// Logisim project 8_bit_computer.circ as structural Verilog: 4 circuits, main circuit main
module main (
);

  EightBitAdder eightbitadder_1 ();  // open: out_5, Cout, B, A, Cin
endmodule

module HalfAdder (
  input  A,
  input  B,
  output Sum,
  output CarryOut
);

  xor xor_1 (Sum, A, B);
  and and_1 (CarryOut, A, B);
endmodule

module FullAdder (
  input  Cin,
  input  A,
  input  B,
  output S,
  output COut
);

  wire halfadder_1_carryout, halfadder_1_sum, halfadder_2_carryout;

  HalfAdder halfadder_1 (.Sum(halfadder_1_sum), .CarryOut(halfadder_1_carryout), .B(B), .A(A));
  HalfAdder halfadder_2 (.Sum(S), .CarryOut(halfadder_2_carryout), .B(Cin), .A(halfadder_1_sum));
  or or_1 (COut, halfadder_1_carryout, halfadder_2_carryout);
endmodule

module EightBitAdder (
  input  [7:0] B,
  input  [7:0] A,
  input  Cin,
  output Cout,
  output [7:0] out_5
);

  wire fulladder_2_cout, fulladder_3_cout, fulladder_4_cout, fulladder_5_cout, fulladder_6_cout,
       fulladder_7_cout, fulladder_8_cout;

  FullAdder fulladder_1 (.COut(Cout), .S(out_5[7]), .Cin(fulladder_2_cout), .A(B[7]), .B(A[7]));
  FullAdder fulladder_2 (.COut(fulladder_2_cout), .S(out_5[6]), .Cin(fulladder_3_cout), .A(B[6]), .B(A[6]));
  FullAdder fulladder_3 (.COut(fulladder_3_cout), .S(out_5[5]), .Cin(fulladder_4_cout), .A(B[5]), .B(A[5]));
  FullAdder fulladder_4 (.COut(fulladder_4_cout), .S(out_5[4]), .Cin(fulladder_5_cout), .A(B[4]), .B(A[4]));
  FullAdder fulladder_5 (.COut(fulladder_5_cout), .S(out_5[3]), .Cin(fulladder_6_cout), .A(B[3]), .B(A[3]));
  FullAdder fulladder_6 (.COut(fulladder_6_cout), .S(out_5[2]), .Cin(fulladder_7_cout), .A(B[2]), .B(A[2]));
  FullAdder fulladder_7 (.COut(fulladder_7_cout), .S(out_5[1]), .Cin(fulladder_8_cout), .A(B[1]), .B(A[1]));
  FullAdder fulladder_8 (.COut(fulladder_8_cout), .S(out_5[0]), .Cin(Cin), .A(B[0]), .B(A[0]));
endmodule
